// Logisim project ULA.circ as structural Verilog: 1 circuit, main circuit ULA
module ULA (
  input  Enable,
  input  [7:0] Numero_1,
  input  [7:0] Numero_2,
  input  [1:0] Cod_Operacao,
  output [7:0] out_5
);

  wire [7:0] AND_out, demultiplexer_1_out0, demultiplexer_1_out1, demultiplexer_1_out2, demultiplexer_2_out0,
       demultiplexer_2_out1, demultiplexer_2_out2, demultiplexer_2_out3, multiplier_1_out, OR_out;

  Demultiplexer #(.select(2), .width(8)) demultiplexer_1 (
    .out0(demultiplexer_1_out0), .out1(demultiplexer_1_out1), .out2(demultiplexer_1_out2), .in(Numero_1),
    .sel(Cod_Operacao), .en(Enable));  // open: out3
  Demultiplexer #(.select(2), .width(8)) demultiplexer_2 (
    .out0(demultiplexer_2_out0), .out1(demultiplexer_2_out1), .out2(demultiplexer_2_out2),
    .out3(demultiplexer_2_out3), .in(Numero_2), .sel(Cod_Operacao), .en(Enable));
  assign AND_out = demultiplexer_1_out0 & demultiplexer_2_out0;  // AND_Gate AND, 8 bits wide
  assign OR_out = demultiplexer_1_out1 | demultiplexer_2_out1;  // OR_Gate OR, 8 bits wide
  Multiplier multiplier_1 (
    .a(demultiplexer_1_out2), .b(demultiplexer_2_out2), .out(multiplier_1_out));  // open: cin, cout
  Multiplexer #(.select(2), .width(8)) multiplexer_1 (
    .in0(AND_out), .in1(OR_out), .in2(multiplier_1_out), .in3(demultiplexer_2_out3), .out(out_5),
    .sel(Cod_Operacao), .en(Enable));

  // Notes on the sheet:
  //   Entradas: Numero 1 e Numero 2
  //   Cod de operaçao: 00 AND
  //   01 OR
  //   10 MUT
  //   11 Copy
endmodule
