// Logisim project bancoRegistradores.circ as structural Verilog: 1 circuit, main circuit Banco de registradores
module Banco_de_registradores (
  input  [7:0] Entrada_1,
  input  [3:0] \Entrada_endereço ,
  input  Enable_entrada_1,
  input  \Enable_saída_1 ,
  input  [3:0] \Saída_1_endereço ,
  input  [7:0] Entrada_2,
  input  [3:0] \Endereço_entrada_2 ,
  input  \Enable_saída_2 ,
  input  Enable_entrada_2,
  input  [3:0] \Saída_2_endereco ,
  input  \Enable_saída_3 ,
  input  [3:0] \Saída_3_endereço ,
  input  Zera,
  input  Clock,
  output [7:0] \Saída_1 ,
  output [7:0] \Saída_2 ,
  output [7:0] out_17
);

  wire undriven_4, undriven_5, undriven_7;
  wire [3:0] undriven_2, undriven_3, undriven_6;
  wire [7:0] demultiplexer_1_out0, demultiplexer_1_out1, demultiplexer_1_out2, demultiplexer_1_out3,
       demultiplexer_1_out4, demultiplexer_1_out5, demultiplexer_1_out6, demultiplexer_1_out7,
       demultiplexer_1_out8, demultiplexer_1_out9, demultiplexer_1_out10, demultiplexer_1_out11,
       demultiplexer_1_out12, demultiplexer_1_out13, demultiplexer_1_out14, demultiplexer_1_out15,
       multiplexer_1_out, multiplexer_2_out, multiplexer_3_out, R0_q, R1_q, R2_q, R3_q, R4_q, R5_q, R6_q,
       R7_q, R8_q, R9_q, R10_q, R11_q, R12_q, R13_q, R14_q, R15_q, undriven;

  Demultiplexer #(.select(4), .width(8)) demultiplexer_1 (
    .out0(demultiplexer_1_out0), .out1(demultiplexer_1_out1), .out2(demultiplexer_1_out2),
    .out3(demultiplexer_1_out3), .out4(demultiplexer_1_out4), .out5(demultiplexer_1_out5),
    .out6(demultiplexer_1_out6), .out7(demultiplexer_1_out7), .out8(demultiplexer_1_out8),
    .out9(demultiplexer_1_out9), .out10(demultiplexer_1_out10), .out11(demultiplexer_1_out11),
    .out12(demultiplexer_1_out12), .out13(demultiplexer_1_out13), .out14(demultiplexer_1_out14),
    .out15(demultiplexer_1_out15), .in(undriven), .sel(\Entrada_endereço ), .en(Enable_entrada_1));
  Demultiplexer #(.select(4), .width(8)) demultiplexer_2 (
    .out0(demultiplexer_1_out0), .out1(demultiplexer_1_out1), .out2(demultiplexer_1_out2),
    .out3(demultiplexer_1_out3), .out4(demultiplexer_1_out4), .out5(demultiplexer_1_out5),
    .out6(demultiplexer_1_out6), .out7(demultiplexer_1_out7), .out8(demultiplexer_1_out8),
    .out9(demultiplexer_1_out9), .out10(demultiplexer_1_out10), .out11(demultiplexer_1_out11),
    .out12(demultiplexer_1_out12), .out13(demultiplexer_1_out13), .out14(demultiplexer_1_out14),
    .out15(demultiplexer_1_out15), .in(Entrada_2), .sel(\Endereço_entrada_2 ), .en(Enable_entrada_2));
  Register R0 (.D(demultiplexer_1_out0), .Q(R0_q), .clk(Clock), .clr(Zera));  // open: en
  Register R1 (.D(demultiplexer_1_out1), .Q(R1_q), .clk(Clock), .clr(Zera));  // open: en
  Register R2 (.D(demultiplexer_1_out2), .Q(R2_q), .clk(Clock), .clr(Zera));  // open: en
  Register R3 (.D(demultiplexer_1_out3), .Q(R3_q), .clk(Clock), .clr(Zera));  // open: en
  Register R4 (.D(demultiplexer_1_out4), .Q(R4_q), .clk(Clock), .clr(Zera));  // open: en
  Register R5 (.D(demultiplexer_1_out5), .Q(R5_q), .clk(Clock), .clr(Zera));  // open: en
  Register R6 (.D(demultiplexer_1_out6), .Q(R6_q), .clk(Clock), .clr(Zera));  // open: en
  Register R7 (.D(demultiplexer_1_out7), .Q(R7_q), .clk(Clock), .clr(Zera));  // open: en
  Register R8 (.D(demultiplexer_1_out8), .Q(R8_q), .clk(Clock), .clr(Zera));  // open: en
  Register R9 (.D(demultiplexer_1_out9), .Q(R9_q), .clk(Clock), .clr(Zera));  // open: en
  Register R10 (.D(demultiplexer_1_out10), .Q(R10_q), .clk(Clock), .clr(Zera));  // open: en
  Register R11 (.D(demultiplexer_1_out11), .Q(R11_q), .clk(Clock), .clr(Zera));  // open: en
  Register R12 (.D(demultiplexer_1_out12), .Q(R12_q), .clk(Clock), .clr(Zera));  // open: en
  Register R13 (.D(demultiplexer_1_out13), .Q(R13_q), .clk(Clock), .clr(Zera));  // open: en
  Register R14 (.D(demultiplexer_1_out14), .Q(R14_q), .clk(Clock), .clr(Zera));  // open: en
  Register R15 (.D(demultiplexer_1_out15), .Q(R15_q), .clk(Clock), .clr(Zera));  // open: en
  Multiplexer #(.select(4), .width(8)) multiplexer_1 (
    .in0(R0_q), .in1(R1_q), .in2(R2_q), .in3(R3_q), .in4(R4_q), .in5(R5_q), .in6(R6_q), .in7(R7_q),
    .in8(R8_q), .in9(R9_q), .in10(R10_q), .in11(R11_q), .in12(R12_q), .in13(R13_q), .in14(R14_q),
    .in15(R15_q), .out(multiplexer_1_out), .sel(undriven_2), .en(undriven_4));
  Multiplexer #(.select(4), .width(8)) multiplexer_2 (
    .in0(R0_q), .in1(R1_q), .in2(R2_q), .in3(R3_q), .in4(R4_q), .in5(R5_q), .in6(R6_q), .in7(R7_q),
    .in8(R8_q), .in9(R9_q), .in10(R10_q), .in11(R11_q), .in12(R12_q), .in13(R13_q), .in14(R14_q),
    .in15(R15_q), .out(multiplexer_2_out), .sel(undriven_3), .en(undriven_5));
  Multiplexer #(.select(4), .width(8)) multiplexer_3 (
    .in0(R0_q), .in1(R1_q), .in2(R2_q), .in3(R3_q), .in4(R4_q), .in5(R5_q), .in6(R6_q), .in7(R7_q),
    .in8(R8_q), .in9(R9_q), .in10(R10_q), .in11(R11_q), .in12(R12_q), .in13(R13_q), .in14(R14_q),
    .in15(R15_q), .out(multiplexer_3_out), .sel(undriven_6), .en(undriven_7));
endmodule
